// Logisim project cpu.circ as structural Verilog: 28 circuits, main circuit main
// CPU
module main (
  input  [31:0] RS_READ_VALUE,
  input  [31:0] RI_READ_VALUE,
  input  [31:0] RD_READ_VALUE,
  input  [31:0] JC_READ_VALUE,
  input  [31:0] INSTRUCTION,
  input  CLOCK,
  output [4:0] RS,
  output [4:0] RI,
  output [4:0] RD,
  output [31:0] RD_WRITE_VALUE,
  output RD_WRITE_ENABLE,
  output [23:0] FETCH_ADDRESS
);

  wire and_1_out, IMMEDIATEMUX, JALENABLE, JUMPENABLE, JUMPTRUE, MEM_LOAD, MEM_WRITE, MEMENABLE, not_2_out,
       u_decode_1_immediateflag, WORD_MODE, WRITE_PERMISSION;
  wire [2:0] u_decode_1_jc;
  wire [3:0] OPCODE, u_decode_1_opcode;
  wire [4:0] u_decode_1_rd, u_decode_1_ri, u_decode_1_rs;
  wire [16:0] u_decode_1_imm;
  wire [23:0] adder_1_out, JUMPADDR, u_decode_1_addr;
  wire [24:0] demultiplexer_1_out1;
  wire [31:0] bit_extender_1_out, demultiplexer_1_out0, IMM, multiplexer_1_out, multiplexer_2_out,
       u_alu_1_alu_result, u_mem_1_data_out;
  wire [31:25] demultiplexer_1_out1_2;

  not not_1 (RD_WRITE_ENABLE, WRITE_PERMISSION);
  u_PC u_pc_1 (.JUMPADDR(JUMPADDR), .JUMPENABLE(JUMPENABLE), .JUMPTRUE(JUMPTRUE), .CLOCK(CLOCK), .PC(FETCH_ADDRESS));
  Multiplexer #(.width(32)) multiplexer_1 (
    .in0(RI_READ_VALUE), .in1(IMM), .out(multiplexer_1_out), .sel(IMMEDIATEMUX));  // open: en
  Adder #(.width(24)) adder_1 (.a(24'h1), .b(FETCH_ADDRESS), .out(adder_1_out));  // open: cin, cout
  u_DECODE u_decode_1 (
    .INSTRUCTION(INSTRUCTION), .OPCODE(u_decode_1_opcode), .IMMEDIATEFLAG(u_decode_1_immediateflag),
    .RD(u_decode_1_rd), .RS(u_decode_1_rs), .RI(u_decode_1_ri), .IMM(u_decode_1_imm), .JC(u_decode_1_jc),
    .ADDR(u_decode_1_addr));
  Multiplexer #(.width(32)) multiplexer_2 (
    .in0(multiplexer_1_out), .in1(bit_extender_1_out), .out(multiplexer_2_out), .sel(JALENABLE));  // open: en
  assign bit_extender_1_out = {{8{1'b0}}, adder_1_out};  // Bit_Extender bit_extender_1
  u_ALU u_alu_1 (
    .ALU_X(RS_READ_VALUE), .ALU_Y(multiplexer_2_out), .ALU_RESULT(u_alu_1_alu_result), .ALU_CONTROL(OPCODE));
  u_CONTROL u_control_1 (
    .OPCODE(u_decode_1_opcode), .IMMEDIATEFLAG(u_decode_1_immediateflag), .RD(u_decode_1_rd),
    .RS(u_decode_1_rs), .RI(u_decode_1_ri), .IMM(u_decode_1_imm), .JC(u_decode_1_jc), .ADDR(u_decode_1_addr),
    .JC_VALUE(JC_READ_VALUE), .JUMPENABLE(JUMPENABLE), .JALENABLE(JALENABLE), .RI_VALUE(RI_READ_VALUE),
    .OPCODE_2(OPCODE), .IMMEDIATEMUX(IMMEDIATEMUX), .RD_2(RD), .RS_2(RS), .RI_2(RI), .IMM_2(IMM),
    .ADDR_2(JUMPADDR), .JUMPTRUE(JUMPTRUE), .MEM_WRITE(MEM_WRITE), .WORD_MODE(WORD_MODE), .MEM_LOAD(MEM_LOAD));
  Demultiplexer #(.width(32)) demultiplexer_1 (
    .out0(demultiplexer_1_out0), .out1({demultiplexer_1_out1_2, demultiplexer_1_out1}),
    .in(u_alu_1_alu_result), .sel(MEMENABLE));  // open: en
  and and_1 (and_1_out, JUMPENABLE, not_2_out);
  or or_1 (WRITE_PERMISSION, and_1_out, MEM_WRITE);
  not not_2 (not_2_out, JALENABLE);
  u_MEM u_mem_1 (
    .ADDRESS(demultiplexer_1_out1), .WORD_MODE(WORD_MODE), .MEM_WRITE(MEM_WRITE), .DATA_IN(RD_READ_VALUE),
    .CLOCK(CLOCK), .DATA_OUT(u_mem_1_data_out));
  or or_2 (MEMENABLE, MEM_WRITE, MEM_LOAD);
  Multiplexer #(.width(32)) multiplexer_3 (
    .in0(demultiplexer_1_out0), .in1(u_mem_1_data_out), .out(RD_WRITE_VALUE), .sel(MEMENABLE));  // open: en

  // Other names for the same wires on the sheet: CLK = CLOCK; FETCHPC[23:0] = FETCH_ADDRESS; JC[31:0] = JC_READ_VALUE;
  //   RD_VALUE[31:0] = RD_READ_VALUE; RD_WRITE[31:0] = RD_WRITE_VALUE; RI_CONTROL[31:0] = RI_READ_VALUE
endmodule

module u_ALU (
  input  [31:0] ALU_X,
  input  [31:0] ALU_Y,
  input  [3:0] ALU_CONTROL,
  output [31:0] ALU_RESULT
);

  wire [31:0] ADD, AND, DIV, MUL, OR, REV, SL, SR, STU, SUB, XOR;

  u_ALU_ADD u_alu_add_1 (.ALU_X(ALU_X), .ALU_Y(ALU_Y), .RESULT(ADD));
  u_ALU_SUB u_alu_sub_1 (.ALU_X(ALU_X), .ALU_Y(ALU_Y), .RESULT(SUB));
  u_ALU_SL u_alu_sl_1 (.ALU_X(ALU_X), .ALU_Y(ALU_Y), .RESULT(SL));
  u_ALU_SR u_alu_sr_1 (.ALU_X(ALU_X), .ALU_Y(ALU_Y), .RESULT(SR));
  u_ALU_AND u_alu_and_1 (.ALU_X(ALU_X), .ALU_Y(ALU_Y), .RESULT(AND));
  u_ALU_OR u_alu_or_1 (.ALU_X(ALU_X), .ALU_Y(ALU_Y), .RESULT(OR));
  u_ALU_REV u_alu_rev_1 (.INPUT(ALU_X), .REVERSE_AMOUNT(ALU_Y[4:0]), .OUTPUT(REV));
  u_ALU_XOR u_alu_xor_1 (.ALU_X(ALU_X), .ALU_Y(ALU_Y), .RESULT(XOR));
  u_ALU_MUL u_alu_mul_1 (.ALU_X(ALU_X), .ALU_Y(ALU_Y), .RESULT(MUL));
  u_ALU_DIVIDE u_alu_divide_1 (.ALU_X(ALU_X), .ALU_Y(ALU_Y), .RESULT(DIV));
  u_ALU_STU u_alu_stu_1 (.ALU_X(ALU_X), .ALU_Y(ALU_Y), .RESULT(STU));
  Multiplexer #(.select(4), .width(32)) multiplexer_1 (
    .in0(SL), .in1(SR), .in2(AND), .in3(OR), .in4(REV), .in5(XOR), .in6(ADD), .in7(SUB), .in8(MUL),
    .in9(DIV), .in10(ADD), .in11(ADD), .in12(ADD), .in13(ADD), .in14(STU), .in15(ALU_Y), .out(ALU_RESULT),
    .sel(ALU_CONTROL));  // open: en

  // Notes on the sheet:
  //   Very simple ALU for now. Calculating all possible operations? Is this a performance lag?
endmodule

// Data Memory
module u_MEM (
  input  [24:0] ADDRESS,
  input  WORD_MODE,
  input  MEM_WRITE,
  input  [31:0] DATA_IN,
  input  CLOCK,
  output [31:0] DATA_OUT
);

  wire not_1_out, not_2_out, not_3_out;
  wire [15:0] EVEN_RESULT, HALF_WORD, LOWER_HALF, multiplexer_1_out, multiplexer_2_out, multiplexer_3_out,
       multiplexer_4_out, multiplexer_7_out, ODD_RESULT, UPPER_HALF;
  wire [23:0] EVEN_ADDR, HALF_EVEN_ADDR, HALF_ODD_ADDR, multiplexer_5_out, multiplexer_6_out, ODD_ADDR;
  wire [24:0] demultiplexer_1_out0, demultiplexer_1_out1;
  wire [31:0] bit_extender_1_out, u_mem_concat_1_result;
  wire [31:16] demultiplexer_2_out0;

  Demultiplexer #(.width(25)) demultiplexer_1 (
    .out0(demultiplexer_1_out0), .out1(demultiplexer_1_out1), .in(ADDRESS), .sel(WORD_MODE));  // open: en
  u_MEM_WORD u_mem_word_1 (.ADDRESS(demultiplexer_1_out1), .EVEN_HALF(HALF_EVEN_ADDR), .ODD_HALF(HALF_ODD_ADDR));
  Demultiplexer #(.width(32)) demultiplexer_2 (
    .out0({demultiplexer_2_out0, HALF_WORD}), .out1({UPPER_HALF, LOWER_HALF}), .in(DATA_IN), .sel(WORD_MODE));  // open: en
  Demultiplexer #(.width(24)) demultiplexer_3 (
    .out0(EVEN_ADDR), .out1(ODD_ADDR), .in(demultiplexer_1_out0[24:1]), .sel(ADDRESS[0]));  // open: en
  Multiplexer #(.width(16)) multiplexer_1 (
    .in0(LOWER_HALF), .in1(UPPER_HALF), .out(multiplexer_1_out), .sel(ADDRESS[0]));  // open: en
  not not_1 (not_1_out, ADDRESS[0]);
  Multiplexer #(.width(16)) multiplexer_2 (
    .in0(LOWER_HALF), .in1(UPPER_HALF), .out(multiplexer_2_out), .sel(not_1_out));  // open: en
  Multiplexer #(.width(16)) multiplexer_3 (
    .in0(HALF_WORD), .in1(multiplexer_1_out), .out(multiplexer_3_out), .sel(WORD_MODE));  // open: en
  Multiplexer #(.width(16)) multiplexer_4 (
    .in0(HALF_WORD), .in1(multiplexer_2_out), .out(multiplexer_4_out), .sel(WORD_MODE));  // open: en
  Multiplexer #(.width(24)) multiplexer_5 (
    .in0(EVEN_ADDR), .in1(HALF_EVEN_ADDR), .out(multiplexer_5_out), .sel(WORD_MODE));  // open: en
  Multiplexer #(.width(24)) multiplexer_6 (
    .in0(ODD_ADDR), .in1(HALF_ODD_ADDR), .out(multiplexer_6_out), .sel(WORD_MODE));  // open: en
  not not_2 (not_2_out, MEM_WRITE);
  Multiplexer #(.width(16)) multiplexer_7 (
    .in0(EVEN_RESULT), .in1(ODD_RESULT), .out(multiplexer_7_out), .sel(ADDRESS[0]));  // open: en
  RAM #(.addrWidth(24), .dataWidth(16), .bus("separate")) ram_1 (
    .addr(multiplexer_5_out), .din(multiplexer_3_out), .data(EVEN_RESULT), .str(MEM_WRITE), .clk(CLOCK),
    .ld(not_2_out));  // open: sel, clr
  RAM #(.addrWidth(24), .dataWidth(16), .bus("separate")) ram_2 (
    .addr(multiplexer_6_out), .din(multiplexer_4_out), .data(ODD_RESULT), .str(MEM_WRITE), .clk(CLOCK),
    .ld(not_3_out));  // open: sel, clr
  not not_3 (not_3_out, MEM_WRITE);
  assign bit_extender_1_out = {{16{multiplexer_7_out[15]}}, multiplexer_7_out};  // Bit_Extender bit_extender_1
  u_MEM_CONCAT u_mem_concat_1 (
    .EVEN_HALF(EVEN_RESULT), .ODD_HALF(ODD_RESULT), .LOWER_IS_EVEN(ADDRESS[0]), .RESULT(u_mem_concat_1_result));
  Multiplexer #(.width(32)) multiplexer_8 (
    .in0(bit_extender_1_out), .in1(u_mem_concat_1_result), .out(DATA_OUT), .sel(WORD_MODE));  // open: en

  // Other names for the same wires on the sheet: EVEN_OR_ODD = ADDRESS[0]; CLK = CLOCK; RESULT[31:0] = DATA_OUT
endmodule

module u_ALU_REV (
  input  [31:0] INPUT,
  input  [4:0] REVERSE_AMOUNT,
  output [31:0] OUTPUT
);

  wire [31:0] multiplexer_1_out, multiplexer_2_out, multiplexer_3_out, multiplexer_4_out,
       u_alu_rev_switch1_1_result, u_alu_rev_switch2_1_result, u_alu_rev_switch3_1_out_2,
       u_alu_rev_switch4_1_out_2, u_alu_rev_switch5_1_out_2;

  u_ALU_REV_SWITCH1 u_alu_rev_switch1_1 (.INPUT(INPUT), .RESULT(u_alu_rev_switch1_1_result));
  Multiplexer #(.width(32)) multiplexer_1 (
    .in0(INPUT), .in1(u_alu_rev_switch1_1_result), .out(multiplexer_1_out), .sel(REVERSE_AMOUNT[0]));  // open: en
  Multiplexer #(.width(32)) multiplexer_2 (
    .in0(multiplexer_1_out), .in1(u_alu_rev_switch2_1_result), .out(multiplexer_2_out),
    .sel(REVERSE_AMOUNT[1]));  // open: en
  u_ALU_REV_SWITCH2 u_alu_rev_switch2_1 (.INPUT(multiplexer_1_out), .RESULT(u_alu_rev_switch2_1_result));
  Multiplexer #(.width(32)) multiplexer_3 (
    .in0(multiplexer_2_out), .in1(u_alu_rev_switch3_1_out_2), .out(multiplexer_3_out), .sel(REVERSE_AMOUNT[2]));  // open: en
  u_ALU_REV_SWITCH3 u_alu_rev_switch3_1 (.in_1(multiplexer_2_out), .out_2(u_alu_rev_switch3_1_out_2));
  Multiplexer #(.width(32)) multiplexer_4 (
    .in0(multiplexer_3_out), .in1(u_alu_rev_switch4_1_out_2), .out(multiplexer_4_out), .sel(REVERSE_AMOUNT[3]));  // open: en
  u_ALU_REV_SWITCH4 u_alu_rev_switch4_1 (.in_1(multiplexer_3_out), .out_2(u_alu_rev_switch4_1_out_2));
  Multiplexer #(.width(32)) multiplexer_5 (
    .in0(multiplexer_4_out), .in1(u_alu_rev_switch5_1_out_2), .out(OUTPUT), .sel(REVERSE_AMOUNT[4]));  // open: en
  u_ALU_REV_SWITCH5 u_alu_rev_switch5_1 (.in_1(multiplexer_4_out), .out_2(u_alu_rev_switch5_1_out_2));

  // Notes on the sheet:
  //   Feel free to use this component, or not, however you want!
endmodule

module u_DECODE (
  input  [31:0] INSTRUCTION,
  output [3:0] OPCODE,
  output IMMEDIATEFLAG,
  output [4:0] RD,
  output [4:0] RS,
  output [4:0] RI,
  output [16:0] IMM,
  output [2:0] JC,
  output [23:0] ADDR
);


  assign ADDR = INSTRUCTION[23:0];
  assign IMM = INSTRUCTION[16:0];
  assign IMMEDIATEFLAG = INSTRUCTION[27];
  assign JC = INSTRUCTION[26:24];
  assign OPCODE = INSTRUCTION[31:28];
  assign RD = INSTRUCTION[26:22];
  assign RI = INSTRUCTION[4:0];
  assign RS = INSTRUCTION[21:17];

  // Other names for the same wires on the sheet: ADDRT[23:0] = INSTRUCTION[23:0];
  //   IMMEDIATET[16:0] = INSTRUCTION[16:0]; INSTRUCT[31:0] = INSTRUCTION; RIT[4:0] = INSTRUCTION[4:0];
  //   RST[4:0] = INSTRUCTION[21:17]; RDT[4:0] = INSTRUCTION[26:22]; JCT[2:0] = INSTRUCTION[26:24];
  //   IMMEDIATEFLAGT = INSTRUCTION[27]; OPCODET[3:0] = INSTRUCTION[31:28]
endmodule

module u_CONTROL (
  input  [3:0] OPCODE,
  input  IMMEDIATEFLAG,
  input  [4:0] RD,
  input  [4:0] RS,
  input  [4:0] RI,
  input  [16:0] IMM,
  input  [2:0] JC,
  input  [23:0] ADDR,
  input  [31:0] RI_VALUE,
  input  [31:0] JC_VALUE,
  output JUMPENABLE,
  output [3:0] OPCODE_2,
  output IMMEDIATEMUX,
  output [4:0] RD_2,
  output [4:0] RS_2,
  output JALENABLE,
  output [4:0] RI_2,
  output [31:0] IMM_2,
  output [23:0] ADDR_2,
  output JUMPTRUE,
  output MEM_WRITE,
  output WORD_MODE,
  output MEM_LOAD
);

  wire comparator_1_eq, comparator_2_eq, comparator_4_eq, comparator_5_eq, comparator_6_eq, comparator_7_eq,
       EQ___GT, EQ___LT, EQZ, GTZ, LQZ, not_1_out;

  Multiplexer #(.width(24)) multiplexer_1 (
    .in0(RI_VALUE[23:0]), .in1(ADDR), .out(ADDR_2), .sel(IMMEDIATEFLAG));  // open: en
  u_SIGNEXTEND17 u_signextend17_1 (.IMMEDIATE17(IMM), .IMMEDIATE32(IMM_2));
  Multiplexer #(.width(5)) multiplexer_2 (.in0(RD), .in1(5'b00110), .out(RD_2), .sel(JALENABLE));  // open: en
  not not_1 (not_1_out, EQZ);
  Comparator #(.width(4)) comparator_1 (.a(4'b1100), .b(OPCODE), .eq(comparator_1_eq));  // open: gt, lt
  Comparator #(.width(4)) comparator_2 (.a(4'b1010), .b(OPCODE), .eq(comparator_2_eq));  // open: gt, lt
  Multiplexer #(.select(3)) multiplexer_3 (
    .in0(1'b1), .in1(GTZ), .in2(EQZ), .in3(LQZ), .in4(EQ___LT), .in5(not_1_out), .in6(EQ___GT), .in7(1'b1),
    .out(JUMPTRUE), .sel(JC));  // open: en
  or or_1 (MEM_LOAD, comparator_1_eq, comparator_2_eq);
  or or_2 (EQ___LT, EQZ, LQZ);
  or or_3 (EQ___GT, EQZ, GTZ);
  Comparator #(.width(32)) comparator_3 (.a(JC_VALUE), .b({32{1'b0}}), .gt(GTZ), .eq(EQZ), .lt(LQZ));
  Comparator #(.width(4)) comparator_4 (.a(4'b1011), .b(OPCODE), .eq(comparator_4_eq));  // open: gt, lt
  Comparator #(.width(4)) comparator_5 (.a(4'b1101), .b(OPCODE), .eq(comparator_5_eq));  // open: gt, lt
  Comparator #(.width(4)) comparator_6 (.a(4'b1100), .b(OPCODE), .eq(comparator_6_eq));  // open: gt, lt
  Comparator #(.width(4)) comparator_7 (.a(4'b1101), .b(OPCODE), .eq(comparator_7_eq));  // open: gt, lt
  and and_1 (JUMPENABLE, OPCODE[3], OPCODE[2], OPCODE[1], OPCODE[0]);
  or or_4 (MEM_WRITE, comparator_4_eq, comparator_5_eq);
  or or_5 (WORD_MODE, comparator_6_eq, comparator_7_eq);
  Comparator #(.width(3)) comparator_8 (.a(3'b111), .b(JC), .eq(JALENABLE));  // open: gt, lt

  assign IMMEDIATEMUX = IMMEDIATEFLAG;
  assign OPCODE_2 = OPCODE;
  assign RI_2 = RI;
  assign RS_2 = RS;

  // Other names for the same wires on the sheet: IMMEDIATE = IMMEDIATEFLAG; JAL = JALENABLE;
  //   RI_VALUE_t[23:0] = RI_VALUE[23:0]

  // Notes on the sheet:
  //   Very Simple for now. Only considering R-Type instructions
  //   All Jump operations and conditions will be included in CONTROL
endmodule

module u_PC (
  input  JUMPENABLE,
  input  JUMPTRUE,
  input  [23:0] JUMPADDR,
  input  CLOCK,
  output [23:0] PC
);

  wire and_1_out;
  wire [23:0] multiplexer_1_out, NEXTPC;

  and and_1 (and_1_out, JUMPENABLE, JUMPTRUE);
  Multiplexer #(.width(24)) multiplexer_1 (
    .in0(NEXTPC), .in1(JUMPADDR), .out(multiplexer_1_out), .sel(and_1_out));  // open: en
  Register #(.width(24)) u_PC (.D(multiplexer_1_out), .Q(PC), .clk(CLOCK));  // open: en, clr
  Adder #(.width(24)) adder_1 (.a(24'h1), .b(PC), .out(NEXTPC));  // open: cin, cout
endmodule

module u_SIGNEXTEND17 (
  input  [16:0] IMMEDIATE17,
  output [31:0] IMMEDIATE32
);

  assign IMMEDIATE32 = {{15{IMMEDIATE17[16]}}, IMMEDIATE17};  // Bit_Extender bit_extender_1
endmodule

module u_ALU_ADD (
  input  [31:0] ALU_X,
  input  [31:0] ALU_Y,
  output [31:0] RESULT
);

  Adder #(.width(32)) adder_1 (.a(ALU_X), .b(ALU_Y), .out(RESULT));  // open: cin, cout
endmodule

module u_ALU_SUB (
  input  [31:0] ALU_X,
  input  [31:0] ALU_Y,
  output [31:0] RESULT
);

  Subtractor #(.width(32)) subtractor_1 (.a(ALU_X), .b(ALU_Y), .out(RESULT));  // open: bin, bout
endmodule

module u_ALU_MUL (
  input  [31:0] ALU_X,
  input  [31:0] ALU_Y,
  output [31:0] RESULT
);

  Multiplier #(.width(32)) multiplier_1 (.a(ALU_X), .b(ALU_Y), .out(RESULT));  // open: cin, cout
endmodule

module u_ALU_SL (
  input  [31:0] ALU_X,
  input  [31:0] ALU_Y,
  output [31:0] RESULT
);

  wire [31:0] CONT, CONT_2, multiplexer_1_out, multiplexer_2_out, u_alu_sl_shiftoneleft_1_result,
       u_alu_sl_shiftoneleft_2_result, u_alu_sl_shiftoneleft_3_result, u_alu_sl_shiftoneleft_4_result,
       u_alu_sl_shiftoneleft_5_result, u_alu_sl_shiftoneleft_6_result, u_alu_sl_shiftoneleft_7_result,
       u_alu_sl_shiftoneleft_8_result, u_alu_sl_shiftoneleft_9_result, u_alu_sl_shiftoneleft_10_result,
       u_alu_sl_shiftoneleft_11_result, u_alu_sl_shiftoneleft_12_result, u_alu_sl_shiftoneleft_13_result,
       u_alu_sl_shiftoneleft_14_result, u_alu_sl_shiftoneleft_15_result, u_alu_sl_shiftoneleft_16_result,
       u_alu_sl_shiftoneleft_17_result, u_alu_sl_shiftoneleft_18_result, u_alu_sl_shiftoneleft_19_result,
       u_alu_sl_shiftoneleft_20_result, u_alu_sl_shiftoneleft_21_result, u_alu_sl_shiftoneleft_22_result,
       u_alu_sl_shiftoneleft_23_result, u_alu_sl_shiftoneleft_24_result, u_alu_sl_shiftoneleft_25_result,
       u_alu_sl_shiftoneleft_26_result, u_alu_sl_shiftoneleft_27_result, u_alu_sl_shiftoneleft_28_result,
       u_alu_sl_shiftoneleft_29_result, u_alu_sl_shiftoneleft_30_result, u_alu_sl_shiftoneleft_31_result;

  u_ALU_SL_SHIFTONELEFT u_alu_sl_shiftoneleft_1 (
    .VALTOSHIFT(u_alu_sl_shiftoneleft_2_result), .RESULT(u_alu_sl_shiftoneleft_1_result));
  u_ALU_SL_SHIFTONELEFT u_alu_sl_shiftoneleft_2 (.VALTOSHIFT(CONT), .RESULT(u_alu_sl_shiftoneleft_2_result));
  u_ALU_SL_SHIFTONELEFT u_alu_sl_shiftoneleft_3 (
    .VALTOSHIFT(u_alu_sl_shiftoneleft_4_result), .RESULT(u_alu_sl_shiftoneleft_3_result));
  u_ALU_SL_SHIFTONELEFT u_alu_sl_shiftoneleft_4 (.VALTOSHIFT(CONT_2), .RESULT(u_alu_sl_shiftoneleft_4_result));
  u_ALU_SL_SHIFTONELEFT u_alu_sl_shiftoneleft_5 (.VALTOSHIFT(ALU_X), .RESULT(u_alu_sl_shiftoneleft_5_result));
  u_ALU_SL_SHIFTONELEFT u_alu_sl_shiftoneleft_6 (
    .VALTOSHIFT(u_alu_sl_shiftoneleft_7_result), .RESULT(u_alu_sl_shiftoneleft_6_result));
  u_ALU_SL_SHIFTONELEFT u_alu_sl_shiftoneleft_7 (
    .VALTOSHIFT(u_alu_sl_shiftoneleft_1_result), .RESULT(u_alu_sl_shiftoneleft_7_result));
  u_ALU_SL_SHIFTONELEFT u_alu_sl_shiftoneleft_8 (
    .VALTOSHIFT(u_alu_sl_shiftoneleft_3_result), .RESULT(u_alu_sl_shiftoneleft_8_result));
  u_ALU_SL_SHIFTONELEFT u_alu_sl_shiftoneleft_9 (
    .VALTOSHIFT(u_alu_sl_shiftoneleft_8_result), .RESULT(u_alu_sl_shiftoneleft_9_result));
  Multiplexer #(.width(32)) multiplexer_1 (
    .in0(ALU_X), .in1(u_alu_sl_shiftoneleft_5_result), .out(multiplexer_1_out), .sel(ALU_Y[0]));  // open: en
  u_ALU_SL_SHIFTONELEFT u_alu_sl_shiftoneleft_10 (
    .VALTOSHIFT(u_alu_sl_shiftoneleft_6_result), .RESULT(u_alu_sl_shiftoneleft_10_result));
  u_ALU_SL_SHIFTONELEFT u_alu_sl_shiftoneleft_11 (
    .VALTOSHIFT(u_alu_sl_shiftoneleft_10_result), .RESULT(u_alu_sl_shiftoneleft_11_result));
  u_ALU_SL_SHIFTONELEFT u_alu_sl_shiftoneleft_12 (
    .VALTOSHIFT(u_alu_sl_shiftoneleft_13_result), .RESULT(u_alu_sl_shiftoneleft_12_result));
  u_ALU_SL_SHIFTONELEFT u_alu_sl_shiftoneleft_13 (
    .VALTOSHIFT(u_alu_sl_shiftoneleft_9_result), .RESULT(u_alu_sl_shiftoneleft_13_result));
  u_ALU_SL_SHIFTONELEFT u_alu_sl_shiftoneleft_14 (
    .VALTOSHIFT(multiplexer_1_out), .RESULT(u_alu_sl_shiftoneleft_14_result));
  u_ALU_SL_SHIFTONELEFT u_alu_sl_shiftoneleft_15 (
    .VALTOSHIFT(u_alu_sl_shiftoneleft_11_result), .RESULT(u_alu_sl_shiftoneleft_15_result));
  u_ALU_SL_SHIFTONELEFT u_alu_sl_shiftoneleft_16 (
    .VALTOSHIFT(u_alu_sl_shiftoneleft_15_result), .RESULT(u_alu_sl_shiftoneleft_16_result));
  u_ALU_SL_SHIFTONELEFT u_alu_sl_shiftoneleft_17 (
    .VALTOSHIFT(u_alu_sl_shiftoneleft_18_result), .RESULT(u_alu_sl_shiftoneleft_17_result));
  u_ALU_SL_SHIFTONELEFT u_alu_sl_shiftoneleft_18 (
    .VALTOSHIFT(u_alu_sl_shiftoneleft_12_result), .RESULT(u_alu_sl_shiftoneleft_18_result));
  Multiplexer #(.width(32)) multiplexer_2 (
    .in0(multiplexer_1_out), .in1(u_alu_sl_shiftoneleft_19_result), .out(multiplexer_2_out), .sel(ALU_Y[1]));  // open: en
  u_ALU_SL_SHIFTONELEFT u_alu_sl_shiftoneleft_19 (
    .VALTOSHIFT(u_alu_sl_shiftoneleft_14_result), .RESULT(u_alu_sl_shiftoneleft_19_result));
  Multiplexer #(.width(32)) multiplexer_3 (
    .in0(CONT), .in1(u_alu_sl_shiftoneleft_16_result), .out(CONT_2), .sel(ALU_Y[3]));  // open: en
  u_ALU_SL_SHIFTONELEFT u_alu_sl_shiftoneleft_20 (
    .VALTOSHIFT(u_alu_sl_shiftoneleft_21_result), .RESULT(u_alu_sl_shiftoneleft_20_result));
  u_ALU_SL_SHIFTONELEFT u_alu_sl_shiftoneleft_21 (
    .VALTOSHIFT(u_alu_sl_shiftoneleft_17_result), .RESULT(u_alu_sl_shiftoneleft_21_result));
  u_ALU_SL_SHIFTONELEFT u_alu_sl_shiftoneleft_22 (
    .VALTOSHIFT(multiplexer_2_out), .RESULT(u_alu_sl_shiftoneleft_22_result));
  u_ALU_SL_SHIFTONELEFT u_alu_sl_shiftoneleft_23 (
    .VALTOSHIFT(u_alu_sl_shiftoneleft_24_result), .RESULT(u_alu_sl_shiftoneleft_23_result));
  u_ALU_SL_SHIFTONELEFT u_alu_sl_shiftoneleft_24 (
    .VALTOSHIFT(u_alu_sl_shiftoneleft_20_result), .RESULT(u_alu_sl_shiftoneleft_24_result));
  u_ALU_SL_SHIFTONELEFT u_alu_sl_shiftoneleft_25 (
    .VALTOSHIFT(u_alu_sl_shiftoneleft_26_result), .RESULT(u_alu_sl_shiftoneleft_25_result));
  u_ALU_SL_SHIFTONELEFT u_alu_sl_shiftoneleft_26 (
    .VALTOSHIFT(u_alu_sl_shiftoneleft_22_result), .RESULT(u_alu_sl_shiftoneleft_26_result));
  u_ALU_SL_SHIFTONELEFT u_alu_sl_shiftoneleft_27 (
    .VALTOSHIFT(u_alu_sl_shiftoneleft_23_result), .RESULT(u_alu_sl_shiftoneleft_27_result));
  u_ALU_SL_SHIFTONELEFT u_alu_sl_shiftoneleft_28 (
    .VALTOSHIFT(u_alu_sl_shiftoneleft_27_result), .RESULT(u_alu_sl_shiftoneleft_28_result));
  u_ALU_SL_SHIFTONELEFT u_alu_sl_shiftoneleft_29 (
    .VALTOSHIFT(u_alu_sl_shiftoneleft_25_result), .RESULT(u_alu_sl_shiftoneleft_29_result));
  u_ALU_SL_SHIFTONELEFT u_alu_sl_shiftoneleft_30 (
    .VALTOSHIFT(u_alu_sl_shiftoneleft_28_result), .RESULT(u_alu_sl_shiftoneleft_30_result));
  u_ALU_SL_SHIFTONELEFT u_alu_sl_shiftoneleft_31 (
    .VALTOSHIFT(u_alu_sl_shiftoneleft_30_result), .RESULT(u_alu_sl_shiftoneleft_31_result));
  Multiplexer #(.width(32)) multiplexer_4 (
    .in0(multiplexer_2_out), .in1(u_alu_sl_shiftoneleft_29_result), .out(CONT), .sel(ALU_Y[2]));  // open: en
  Multiplexer #(.width(32)) multiplexer_5 (
    .in0(CONT_2), .in1(u_alu_sl_shiftoneleft_31_result), .out(RESULT), .sel(ALU_Y[4]));  // open: en

  // Other names for the same wires on the sheet: SHIFT_1 = ALU_Y[0]; SHIFT_2 = ALU_Y[1]; SHIFT_4 = ALU_Y[2];
  //   SHIFT_8 = ALU_Y[3]; SHIFT_16 = ALU_Y[4]
endmodule

module u_ALU_SL_SHIFTONELEFT (
  input  [31:0] VALTOSHIFT,
  output [31:0] RESULT
);


  assign RESULT = {VALTOSHIFT[30:0], VALTOSHIFT[0]};
endmodule

module u_ALU_SR (
  input  [31:0] ALU_X,
  input  [31:0] ALU_Y,
  output [31:0] RESULT
);

  Shifter #(.width(32), .shift("ar")) shifter_1 (.in(ALU_X), .\dist (ALU_Y[4:0]), .out(RESULT));
endmodule

module u_ALU_AND (
  input  [31:0] ALU_X,
  input  [31:0] ALU_Y,
  output [31:0] RESULT
);

  assign RESULT = ALU_X & ALU_Y;  // AND_Gate and_1, 32 bits wide
endmodule

module u_ALU_OR (
  input  [31:0] ALU_X,
  input  [31:0] ALU_Y,
  output [31:0] RESULT
);

  assign RESULT = ALU_X | ALU_Y;  // OR_Gate or_1, 32 bits wide
endmodule

module u_ALU_XOR (
  input  [31:0] ALU_X,
  input  [31:0] ALU_Y,
  output [31:0] RESULT
);

  assign RESULT = ALU_X ^ ALU_Y;  // XOR_Gate xor_1, 32 bits wide
endmodule

module u_ALU_DIVIDE (
  input  [31:0] ALU_X,
  input  [31:0] ALU_Y,
  output [31:0] RESULT
);

  wire ALU_X_EQ, ALU_Y_EQ, CHECK, comparator_5_eq, comparator_6_eq, EQ, GT, LT;
  wire [1:0] multiplexer_2_out, multiplexer_4_out;
  wire [30:0] divider_1_out, multiplexer_1_out, multiplexer_5_out, u_alu_divide_invertaddone_1_output,
       u_alu_divide_invertaddone_2_output, u_alu_divide_invertaddone_3_output;
  wire [31:0] bit_extender_1_out, bit_extender_2_out, demultiplexer_1_out0, demultiplexer_1_out1,
       demultiplexer_2_out0, demultiplexer_2_out1, demultiplexer_3_out0, demultiplexer_3_out1, divider_2_out,
       multiplexer_3_out, multiplexer_6_out, multiplexer_7_out, multiplexer_8_out, multiplexer_11_out,
       RESULTREG, RESULTSPEC, u_alu_divide_invertaddone32_1_output;

  Comparator #(.width(32)) comparator_1 (.a(32'h80000000), .b(ALU_X), .eq(ALU_X_EQ));  // open: gt, lt
  Demultiplexer #(.width(32)) demultiplexer_1 (
    .out0(demultiplexer_1_out0), .out1(demultiplexer_1_out1), .in(ALU_Y), .sel(CHECK));  // open: en
  Demultiplexer #(.width(32)) demultiplexer_2 (
    .out0(demultiplexer_2_out0), .out1(demultiplexer_2_out1), .in(ALU_X), .sel(ALU_X_EQ));  // open: en
  Demultiplexer #(.width(32)) demultiplexer_3 (
    .out0(demultiplexer_3_out0), .out1(demultiplexer_3_out1), .in(ALU_Y), .sel(ALU_Y_EQ));  // open: en
  Comparator #(.width(32)) comparator_2 (.a({32{1'b0}}), .b(ALU_Y), .eq(CHECK));  // open: gt, lt
  u_ALU_DIVIDE_INVERTADDONE u_alu_divide_invertaddone_1 (
    .Input(demultiplexer_2_out0[30:0]), .Output(u_alu_divide_invertaddone_1_output));
  Comparator #(.width(32)) comparator_3 (.a(32'h80000000), .b(demultiplexer_1_out0), .eq(ALU_Y_EQ));  // open: gt, lt
  Comparator #(.width(32)) comparator_4 (.a({32{1'b0}}), .b(ALU_X), .gt(LT), .eq(EQ), .lt(GT));
  assign bit_extender_1_out = {{1{1'b0}}, multiplexer_5_out};  // Bit_Extender bit_extender_1
  Comparator #(.width(32)) comparator_5 (.a(ALU_X), .b(demultiplexer_3_out1), .eq(comparator_5_eq));  // open: gt, lt
  Multiplexer #(.width(31)) multiplexer_1 (
    .in0(demultiplexer_2_out0[30:0]), .in1(u_alu_divide_invertaddone_1_output), .out(multiplexer_1_out),
    .sel(demultiplexer_2_out0[31]));  // open: en
  Divider #(.width(31)) divider_1 (
    .a(multiplexer_1_out), .b(multiplexer_5_out), .out(divider_1_out));  // open: upper, rem
  Multiplexer #(.width(2)) multiplexer_2 (
    .in0(2'b01), .in1(2'b00), .out(multiplexer_2_out), .sel(ALU_X_EQ));  // open: en
  Multiplexer #(.width(32)) multiplexer_3 (
    .in0(demultiplexer_1_out1), .in1({32{1'b0}}), .out(multiplexer_3_out), .sel(EQ));  // open: en
  u_ALU_DIVIDE_INVERTADDONE u_alu_divide_invertaddone_2 (
    .Input(demultiplexer_3_out0[30:0]), .Output(u_alu_divide_invertaddone_2_output));
  Divider #(.width(32)) divider_2 (
    .a(demultiplexer_2_out1), .b(bit_extender_1_out), .out(divider_2_out));  // open: upper, rem
  Multiplexer #(.width(2)) multiplexer_4 (
    .in0(multiplexer_2_out), .in1(2'b10), .out(multiplexer_4_out), .sel(ALU_Y_EQ));  // open: en
  Multiplexer #(.width(31)) multiplexer_5 (
    .in0(demultiplexer_3_out0[30:0]), .in1(u_alu_divide_invertaddone_2_output), .out(multiplexer_5_out),
    .sel(demultiplexer_3_out0[31]));  // open: en
  xor xor_1 (multiplexer_8_out[31], demultiplexer_2_out0[31], demultiplexer_3_out0[31]);
  assign bit_extender_2_out = {{31{1'b0}}, comparator_5_eq};  // Bit_Extender bit_extender_2
  Comparator #(.width(32)) comparator_6 (
    .a(multiplexer_8_out), .b(32'h80000000), .eq(comparator_6_eq));  // open: gt, lt
  u_ALU_DIVIDE_INVERTADDONE u_alu_divide_invertaddone_3 (
    .Input(divider_1_out), .Output(u_alu_divide_invertaddone_3_output));
  Multiplexer #(.width(32)) multiplexer_6 (
    .in0(multiplexer_8_out), .in1({32{1'b0}}), .out(multiplexer_6_out), .sel(comparator_6_eq));  // open: en
  Multiplexer #(.width(32)) multiplexer_7 (
    .in0(multiplexer_3_out), .in1(32'h7fffffff), .out(multiplexer_7_out), .sel(GT));  // open: en
  Multiplexer #(.width(31)) multiplexer_8 (
    .in0(divider_1_out), .in1(u_alu_divide_invertaddone_3_output), .out(multiplexer_8_out[30:0]),
    .sel(multiplexer_8_out[31]));  // open: en
  Multiplexer #(.select(2), .width(32)) multiplexer_9 (
    .in0(multiplexer_11_out), .in1(multiplexer_6_out), .in2(bit_extender_2_out), .out(RESULTREG),
    .sel(multiplexer_4_out));  // open: in3, en
  u_ALU_DIVIDE_INVERTADDONE32 u_alu_divide_invertaddone32_1 (
    .Input(divider_2_out), .Output(u_alu_divide_invertaddone32_1_output));
  Multiplexer #(.width(32)) multiplexer_10 (
    .in0(multiplexer_7_out), .in1(32'h80000000), .out(RESULTSPEC), .sel(LT));  // open: en
  Multiplexer #(.width(32)) multiplexer_11 (
    .in0(u_alu_divide_invertaddone32_1_output), .in1(divider_2_out), .out(multiplexer_11_out),
    .sel(demultiplexer_3_out0[31]));  // open: en
  Multiplexer #(.width(32)) multiplexer_12 (.in0(RESULTREG), .in1(RESULTSPEC), .out(RESULT), .sel(CHECK));  // open: en
endmodule

module u_ALU_STU (
  input  [31:0] ALU_X,
  input  [31:0] ALU_Y,
  output [31:0] RESULT
);


  assign RESULT = {ALU_Y[16:0], ALU_X[14:0]};

  // Notes on the sheet:
  //   Get Lower 17 bits (Actual Immediate)
endmodule

module u_MEM_WORD (
  input  [24:0] ADDRESS,
  output [23:0] EVEN_HALF,
  output [23:0] ODD_HALF
);

  wire [23:0] LOWER_EVEN_HALF, LOWER_ODD_HALF, UPPER_EVEN_HALF, UPPER_ODD_HALF;
  wire [24:0] UPPER_HALF;

  Adder #(.width(25)) adder_1 (.a(25'h1), .b(ADDRESS), .out(UPPER_HALF));  // open: cin, cout
  Demultiplexer #(.width(24)) demultiplexer_1 (
    .out0(LOWER_EVEN_HALF), .out1(LOWER_ODD_HALF), .in(ADDRESS[24:1]), .sel(ADDRESS[0]));  // open: en
  Multiplexer #(.width(24)) multiplexer_1 (
    .in0(LOWER_EVEN_HALF), .in1(UPPER_EVEN_HALF), .out(EVEN_HALF), .sel(ADDRESS[0]));  // open: en
  Multiplexer #(.width(24)) multiplexer_2 (
    .in0(UPPER_ODD_HALF), .in1(LOWER_ODD_HALF), .out(ODD_HALF), .sel(ADDRESS[0]));  // open: en
  Demultiplexer #(.width(24)) demultiplexer_2 (
    .out0(UPPER_ODD_HALF), .out1(UPPER_EVEN_HALF), .in(UPPER_HALF[24:1]), .sel(ADDRESS[0]));  // open: en

  // Other names for the same wires on the sheet: ADDR[24:0] = ADDRESS; ODD = ADDRESS[0]
endmodule

module u_MEM_CONCAT (
  input  [15:0] EVEN_HALF,
  input  [15:0] ODD_HALF,
  input  LOWER_IS_EVEN,
  output [31:0] RESULT
);

  wire not_1_out;

  not not_1 (not_1_out, LOWER_IS_EVEN);
  Multiplexer #(.width(16)) multiplexer_1 (
    .in0(EVEN_HALF), .in1(ODD_HALF), .out(RESULT[15:0]), .sel(LOWER_IS_EVEN));  // open: en
  Multiplexer #(.width(16)) multiplexer_2 (
    .in0(EVEN_HALF), .in1(ODD_HALF), .out(RESULT[31:16]), .sel(not_1_out));  // open: en
endmodule

module u_ALU_DIVIDE_INVERTADDONE (
  input  [30:0] Input,
  output [30:0] Output
);

  wire [30:0] not_1_out;

  assign not_1_out = ~Input;  // NOT_Gate not_1, 31 bits wide
  Adder #(.width(31)) adder_1 (.a(not_1_out), .b(31'h1), .out(Output));  // open: cin, cout
endmodule

module u_ALU_DIVIDE_INVERTADDONE32 (
  input  [31:0] Input,
  output [31:0] Output
);

  wire [31:0] not_1_out;

  assign not_1_out = ~Input;  // NOT_Gate not_1, 32 bits wide
  Adder #(.width(32)) adder_1 (.a(not_1_out), .b(32'h1), .out(Output));  // open: cin, cout
endmodule

module u_ALU_REV_SWITCH1 (
  input  [31:0] INPUT,
  output [31:0] RESULT
);


  assign RESULT = {INPUT[30], INPUT[31], INPUT[28], INPUT[29], INPUT[26], INPUT[27], INPUT[24], INPUT[25], INPUT[22], INPUT[23], INPUT[20], INPUT[21], INPUT[18], INPUT[19], INPUT[16], INPUT[17], INPUT[14], INPUT[15], INPUT[12], INPUT[13], INPUT[10], INPUT[11], INPUT[8], INPUT[9], INPUT[6], INPUT[7], INPUT[4], INPUT[5], INPUT[2], INPUT[3], INPUT[0], INPUT[1]};
endmodule

module u_ALU_REV_SWITCH2 (
  input  [31:0] INPUT,
  output [31:0] RESULT
);


  assign RESULT = {INPUT[29:28], INPUT[31:30], INPUT[25:24], INPUT[27:26], INPUT[21:20], INPUT[23:22], INPUT[17:16], INPUT[19:18], INPUT[13:12], INPUT[15:14], INPUT[9:8], INPUT[11:10], INPUT[5:4], INPUT[7:6], INPUT[1:0], INPUT[3:2]};
endmodule

module u_ALU_REV_SWITCH3 (
  input  [31:0] in_1,
  output [31:0] out_2
);


  assign out_2 = {in_1[27:24], in_1[31:28], in_1[19:16], in_1[23:20], in_1[11:8], in_1[15:12], in_1[3:0], in_1[7:4]};

  // Other names for the same wires on the sheet: _4 = in_1[4]; _5 = in_1[5]; _6 = in_1[6]; _7 = in_1[7]; _0 = in_1[0];
  //   _1 = in_1[1]; _2 = in_1[2]; _3 = in_1[3]; _12 = in_1[12]; _13 = in_1[13]; _14 = in_1[14]; _15 = in_1[15];
  //   _8 = in_1[8]; _9 = in_1[9]; _10 = in_1[10]; _11 = in_1[11]; _20 = in_1[20]; _21 = in_1[21]; _22 = in_1[22];
  //   _23 = in_1[23]; _16 = in_1[16]; _17 = in_1[17]; _18 = in_1[18]; _19 = in_1[19]; _28 = in_1[28]; _29 = in_1[29];
  //   _30 = in_1[30]; _31 = in_1[31]; _24 = in_1[24]; _25 = in_1[25]; _26 = in_1[26]; _27 = in_1[27]
endmodule

module u_ALU_REV_SWITCH4 (
  input  [31:0] in_1,
  output [31:0] out_2
);


  assign out_2 = {in_1[23:16], in_1[31:24], in_1[7:0], in_1[15:8]};

  // Other names for the same wires on the sheet: _8 = in_1[8]; _9 = in_1[9]; _10 = in_1[10]; _11 = in_1[11];
  //   _12 = in_1[12]; _13 = in_1[13]; _14 = in_1[14]; _15 = in_1[15]; _0 = in_1[0]; _1 = in_1[1]; _2 = in_1[2];
  //   _3 = in_1[3]; _4 = in_1[4]; _5 = in_1[5]; _6 = in_1[6]; _7 = in_1[7]; _24 = in_1[24]; _25 = in_1[25];
  //   _26 = in_1[26]; _27 = in_1[27]; _28 = in_1[28]; _29 = in_1[29]; _30 = in_1[30]; _31 = in_1[31]; _16 = in_1[16];
  //   _17 = in_1[17]; _18 = in_1[18]; _19 = in_1[19]; _20 = in_1[20]; _21 = in_1[21]; _22 = in_1[22]; _23 = in_1[23]
endmodule

module u_ALU_REV_SWITCH5 (
  input  [31:0] in_1,
  output [31:0] out_2
);


  assign out_2 = {in_1[15:0], in_1[31:16]};

  // Other names for the same wires on the sheet: _16 = in_1[16]; _17 = in_1[17]; _18 = in_1[18]; _19 = in_1[19];
  //   _20 = in_1[20]; _21 = in_1[21]; _22 = in_1[22]; _23 = in_1[23]; _24 = in_1[24]; _25 = in_1[25]; _26 = in_1[26];
  //   _27 = in_1[27]; _28 = in_1[28]; _29 = in_1[29]; _30 = in_1[30]; _31 = in_1[31]; _0 = in_1[0]; _1 = in_1[1];
  //   _2 = in_1[2]; _3 = in_1[3]; _4 = in_1[4]; _5 = in_1[5]; _6 = in_1[6]; _7 = in_1[7]; _8 = in_1[8]; _9 = in_1[9];
  //   _10 = in_1[10]; _11 = in_1[11]; _12 = in_1[12]; _13 = in_1[13]; _14 = in_1[14]; _15 = in_1[15]
endmodule
